# Fritzing sketch ROBOT_TANK_RACER_SCHEMATICS (saved by Fritzing 0.9.3b)

parts:
  L298N1 = L298N DC motor driver
  Componente1 = Arduino Uno (Rev3) - ICSP
  LED_STATUS = LEDs [package=led10mm]
  LED_ON = smd LED [color="Red (660nm)" package="0805 [SMD]"]
  LED_YELLOW = smd LED [color="Yellow (595nm)" package="0805 [SMD]"]
  LED_BLUE = smd LED [color="Blue (430nm)" package="0805 [SMD]"]
  S1 = Round Pushbutton
  INPUT_YELLOW = Header 2 [package=screwterminal-3.5mm-2_lock]
  INPUT_BLUE = Header 2 [package=screwterminal-3.5mm-2_lock]
  ENG2_TANK = DC Motor
  SENSOR_YELLOW = CAPSENSE_PAD [package=capsense_pad]
  SENSOR_BLUE = CAPSENSE_PAD [package=capsense_pad]
  ENG1_TANK = DC Motor
  J2 = Power Jack [package=power_jack_pth]

nets:
  N1: L298N1.OUT1, ENG2_TANK.pin_2
  N2: L298N1.OUT2, ENG2_TANK.pin_1
  N3: L298N1.OUT3, ENG1_TANK.pin_2
  N4: L298N1.OUT4, ENG1_TANK.pin_1
  N5: L298N1.12V, J2.PWR
  GND: L298N1.GND, Componente1.GND, LED_STATUS.C, LED_ON.cathode, LED_YELLOW.cathode, LED_BLUE.cathode, S1.leg0, INPUT_YELLOW.1, INPUT_BLUE.1, J2.GND
  5V: L298N1.5V, Componente1.VIN
  N6: Componente1.A0, S1.leg1
  N7: Componente1.A2, INPUT_BLUE.2
  N8: Componente1.A3, INPUT_YELLOW.2
  N9: Componente1.A4/SDA, SENSOR_BLUE.RECEIVE
  N10: Componente1.A5/SCL, SENSOR_YELLOW.RES
  N11: Componente1.ICSP_MISO, Componente1.D12/MISO, LED_ON.anode
  N12: Componente1.D8, LED_YELLOW.anode
  N13: Componente1.D9_PWM, LED_BLUE.anode
  N14: Componente1.D13/SCK, LED_STATUS.A

notes:
  These are the 2 motors of the Tank. Pay atention to the way you should connect the wires, your motors can be in a diferent position, so you would have to change this configuration.
  This GND goes to the extremities of the tank to complete the circuit when it touches SENSOR_YELLOW or SENSOR_BLUE

custom parts:
  L298N DC motor driver: 2x DC motor driver with 78M05 positive voltage regulator (7..35 V) L298N: max 46 V, 2 A Set 5 V Enable jumper to enable 5 V regultor (needed for the L298N) and +5 V output at screw terminal or supply external +5 V at screw terminal Set ENA and/or ENB to +5 V to enable motor permanently or supply ENA and/or ENB with PWM signal IN1 and IN2 set rotation directory for motor A (OUT1/OUT2) IN2 and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
  Power Jack: Power Jack This is the standard 5.5mm barrel jack for power. The PTH is the most common, proven, reliable, footprint. All others are experimental. The Slot footprint only works if the mill layer is transmitted to the PCB fab house so be warned. Spark Fun Electronics SKU : PRT-00119. Mating wall wart : TOL-00298 (and others)
